# Fritzing sketch DAKT3 (saved by Fritzing 0.9.3b)

parts:
  Part1 = KY-019 5V Relay Module [package="Breakout board"]
  Mod1 = zmpt101b
  Part2 = LCD1602-I2C
  Part3 = Current Sensor 5A
  S1 = Round Pushbutton
  S2 = Round Pushbutton
  S3 = Round Pushbutton
  U1 = ESP32S-HiLetgo [part_number=ESP32S-HiLetgo]

nets:
  N1: Part1.S, U1.GPIO32
  N2: Mod1.OUT, U1.GPIO35
  GND: Part2.GND, U1.GND
  VCC: Part2.VCC, U1.VIN
  N3: Part2.SDA, U1.GPIO21
  N4: Part2.SCL, U1.GPIO22
  N5: Part3.2, Part3.OUT, U1.GPIO34
  N6: S1.leg0, U1.3.3
  N7: S1.leg1, U1.GPIO19
  N8: S2.leg1, U1.GPIO5
  N9: S3.leg1, U1.GPIO18

custom parts:
  KY-019 5V Relay Module: KY-019 5V Relay module, used to control AC circuits.
  zmpt101b: Single phase ac active output voltate transformer module.
  LCD1602-I2C: A standard character display, usually with 2x16 characters. Comes in many colors with LCM1602 IIC attached.
  ESP32S-HiLetgo: HiLetgo ESP-WROOM-32 ESP32 ESP-32S Development Board 2.4GHz Dual-Mode WiFi + Bluetooth Dual Cores Microcontroller The ESP32 integrated with Antenna switches, RF Balun, power amplifiers, low-noise amplifiers, filters, and management modules, and the entire solution occupies the least area of PCB. 2.4 GHz Wi-Fi plus Bluetooth dual-mode chip, with TSMC Ultra-low power consumption 40nm technology,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
